// Logisim project ALU DECODER.circ as structural Verilog: 1 circuit, main circuit ALU DECODER
module ALU_DECODER (
  input  ALUOp,
  input  [5:0] Func_5_0,
  output [1:0] FlagW_1_0,
  output [1:0] out_4
);

  wire and_2_out, and_3_out, and_4_out, and_5_out;

  and and_1 (FlagW_1_0[1], ALUOp, Func_5_0[0]);
  and and_2 (and_2_out, ALUOp, ~Func_5_0[1], Func_5_0[2], ~Func_5_0[3], ~Func_5_0[4]);  // AND_Gate
  and and_3 (and_3_out, ALUOp, ~Func_5_0[1], ~Func_5_0[2], Func_5_0[3], Func_5_0[4]);  // AND_Gate
  and and_4 (and_4_out, ALUOp, ~Func_5_0[1], ~Func_5_0[2], ~Func_5_0[3], ~Func_5_0[4]);  // AND_Gate
  and and_5 (and_5_out, ALUOp, ~Func_5_0[1], ~Func_5_0[2], Func_5_0[3], Func_5_0[4]);  // AND_Gate
  or or_1 (out_4[0], and_2_out, and_3_out);
  or or_2 (out_4[1], and_4_out, and_5_out);
  and and_6 (FlagW_1_0[0], FlagW_1_0[1], ~out_4[1]);  // AND_Gate

  // Notes on the sheet:
  //   ALUControl 1:0
endmodule
