// Logisim project ARM_CPU_FARIDA_ALIYEVA.circ as structural Verilog: 12 circuits, main circuit ARM_CPU_SINGLE
module ARM_CPU_SINGLE (
);

  wire button_1_out, clock_1_out, control_unit_1_alusrc, control_unit_1_memtoreg, control_unit_1_memwrite,
       control_unit_1_pcsrc, control_unit_1_regwrite;
  wire [1:0] control_unit_1_alucontrol1_0, control_unit_1_immsrc1_0, control_unit_1_regsrc1_0, rom_1_data_7,
       rom_1_data_8;
  wire [3:0] alu_1_alu_flags, multiplexer_2_out, multiplexer_3_out, rom_1_data, rom_1_data_2, rom_1_data_3,
       rom_1_data_4, rom_1_data_5, rom_1_data_6, rom_1_data_9;
  wire [31:0] adder_1_out, adder_2_out, alu_1_alu_result, data_memory_1_out_6, extender_1_out_5,
       multiplexer_1_out, multiplexer_4_out, multiplexer_5_out, register_1_q, register_file_1_rd1,
       register_file_1_rd2;

  Clock clock_1 (.out(clock_1_out));
  Button button_1 (.out(button_1_out));
  Multiplexer #(.width(32), .enable("false")) multiplexer_1 (
    .in0(adder_1_out), .in1(multiplexer_5_out), .out(multiplexer_1_out), .sel(control_unit_1_pcsrc));
  Register #(.width(32)) register_1 (
    .D(multiplexer_1_out), .Q(register_1_q), .clk(clock_1_out), .clr(button_1_out));  // open: en
  Adder #(.width(32)) adder_1 (.a(register_1_q), .b(32'h4), .out(adder_1_out));  // open: cin, cout
  ROM #(.dataWidth(32)) rom_1 (
    .addr(register_1_q[7:0]),
    .data({rom_1_data_9, rom_1_data_8, rom_1_data_7, rom_1_data_6, rom_1_data_5, rom_1_data_4, rom_1_data_3, rom_1_data_2, rom_1_data}));  // open: sel
  Control_Unit control_unit_1 (
    .Cond_3_0(rom_1_data_9), .ALU_Flags_3_0(alu_1_alu_flags), .Rd3_0(rom_1_data_4), .Op1_0(rom_1_data_8),
    .Funct5_0({rom_1_data_7, rom_1_data_6}), .CLK(clock_1_out), .CLR(button_1_out),
    .PCSrc(control_unit_1_pcsrc), .RegWrite(control_unit_1_regwrite), .MemWrite(control_unit_1_memwrite),
    .MemtoReg(control_unit_1_memtoreg), .ALUSrc(control_unit_1_alusrc), .ImmSrc1_0(control_unit_1_immsrc1_0),
    .RegSrc1_0(control_unit_1_regsrc1_0), .ALUControl1_0(control_unit_1_alucontrol1_0));
  Multiplexer #(.width(4), .enable("false")) multiplexer_2 (
    .in0(rom_1_data_5), .in1(4'b1111), .out(multiplexer_2_out), .sel(control_unit_1_regsrc1_0[0]));
  Adder #(.width(32)) adder_2 (.a(32'h4), .b(adder_1_out), .out(adder_2_out));  // open: cin, cout
  Multiplexer #(.width(4), .enable("false")) multiplexer_3 (
    .in0(rom_1_data), .in1(rom_1_data_4), .out(multiplexer_3_out), .sel(control_unit_1_regsrc1_0[1]));
  Extender extender_1 (
    .in_1(control_unit_1_immsrc1_0), .in_2({rom_1_data_2, rom_1_data}),
    .in_3({rom_1_data_3, rom_1_data_2, rom_1_data}),
    .in_4({rom_1_data_6, rom_1_data_5, rom_1_data_4, rom_1_data_3, rom_1_data_2, rom_1_data}),
    .out_5(extender_1_out_5));
  Register_File register_file_1 (
    .WD3(multiplexer_5_out), .clk(clock_1_out), .clr(button_1_out), .WE3(control_unit_1_regwrite),
    .A3(rom_1_data_4), .R15(adder_2_out), .A1(multiplexer_2_out), .A2(multiplexer_3_out),
    .RD1(register_file_1_rd1), .RD2(register_file_1_rd2));
  Multiplexer #(.width(32), .enable("false")) multiplexer_4 (
    .in0(register_file_1_rd2), .in1(extender_1_out_5), .out(multiplexer_4_out), .sel(control_unit_1_alusrc));
  Data_Memory data_memory_1 (
    .WE(control_unit_1_memwrite), .ALUResult(alu_1_alu_result), .WriteData(register_file_1_rd2),
    .CLR(button_1_out), .CLK(clock_1_out), .out_6(data_memory_1_out_6));
  ALU alu_1 (
    .ALUControl(control_unit_1_alucontrol1_0), .A(register_file_1_rd1), .B(multiplexer_4_out),
    .ALU_Result(alu_1_alu_result), .ALU_Flags(alu_1_alu_flags));
  Multiplexer #(.width(32), .enable("false")) multiplexer_5 (
    .in0(alu_1_alu_result), .in1(data_memory_1_out_6), .out(multiplexer_5_out), .sel(control_unit_1_memtoreg));

  // Notes on the sheet:
  //   contents of rom_1 (hex, n*v repeats v):
  //   e2506004 0 0 0 a000005 0 0 0 e5951000 0 0 0 e2811008 0 0 0 e5851000 0 0 0 e2855004 0 0 0 e2800001 0
  //   0 0 eafffff7 0 0 0 eafffffe
  //   Control Unit
  //   Extender
  //   Register File
  //   Data Memory
  //   ALU
  //   FARIDA ALIYEVA
endmodule

module Data_Memory (
  input  WE,
  input  [31:0] ALUResult,
  input  [31:0] WriteData,
  input  CLR,
  input  CLK,
  output [31:0] out_6
);

  wire not_1_out;

  RAM #(.dataWidth(32), .bus("separate")) ram_1 (
    .addr(ALUResult[9:2]), .din(WriteData), .data(out_6), .str(WE), .clk(CLK), .ld(not_1_out), .clr(CLR));  // open: sel
  not not_1 (not_1_out, WE);
endmodule

module Register_File (
  input  [31:0] WD3,
  input  clk,
  input  clr,
  input  [3:0] A1,
  input  [3:0] A2,
  input  [31:0] R15,
  input  WE3,
  input  [3:0] A3,
  output [31:0] RD1,
  output [31:0] RD2
);

  wire decoder_1_out0, decoder_1_out1, decoder_1_out2, decoder_1_out3, decoder_1_out4, decoder_1_out5,
       decoder_1_out6, decoder_1_out7, decoder_1_out8, decoder_1_out9, decoder_1_out10, decoder_1_out11,
       decoder_1_out12, decoder_1_out13, decoder_1_out14;
  wire [31:0] R0_q, R1_q, R2_q, R3_q, R4_q, R5_q, R6_q, R7_q, R8_q, R9_q, R10_q, R11_q, R12_q, R13_q, R14_q;

  Decoder_part #(.select(4), .disabled(0)) decoder_1 (
    .out0(decoder_1_out0), .out1(decoder_1_out1), .out2(decoder_1_out2), .out3(decoder_1_out3),
    .out4(decoder_1_out4), .out5(decoder_1_out5), .out6(decoder_1_out6), .out7(decoder_1_out7),
    .out8(decoder_1_out8), .out9(decoder_1_out9), .out10(decoder_1_out10), .out11(decoder_1_out11),
    .out12(decoder_1_out12), .out13(decoder_1_out13), .out14(decoder_1_out14), .sel(A3), .en(WE3));  // open: out15
  Register #(.width(32)) R14 (.D(WD3), .en(decoder_1_out14), .Q(R14_q), .clk(clk), .clr(clr));
  Register #(.width(32)) R13 (.D(WD3), .en(decoder_1_out13), .Q(R13_q), .clk(clk), .clr(clr));
  Register #(.width(32)) R11 (.D(WD3), .en(decoder_1_out11), .Q(R11_q), .clk(clk), .clr(clr));
  Register #(.width(32)) R12 (.D(WD3), .en(decoder_1_out12), .Q(R12_q), .clk(clk), .clr(clr));
  Register #(.width(32)) R10 (.D(WD3), .en(decoder_1_out10), .Q(R10_q), .clk(clk), .clr(clr));
  Register #(.width(32)) R9 (.D(WD3), .en(decoder_1_out9), .Q(R9_q), .clk(clk), .clr(clr));
  Register #(.width(32)) R7 (.D(WD3), .en(decoder_1_out7), .Q(R7_q), .clk(clk), .clr(clr));
  Register #(.width(32)) R8 (.D(WD3), .en(decoder_1_out8), .Q(R8_q), .clk(clk), .clr(clr));
  Register #(.width(32)) R6 (.D(WD3), .en(decoder_1_out6), .Q(R6_q), .clk(clk), .clr(clr));
  Register #(.width(32)) R5 (.D(WD3), .en(decoder_1_out5), .Q(R5_q), .clk(clk), .clr(clr));
  Register #(.width(32)) R4 (.D(WD3), .en(decoder_1_out4), .Q(R4_q), .clk(clk), .clr(clr));
  Register #(.width(32)) R3 (.D(WD3), .en(decoder_1_out3), .Q(R3_q), .clk(clk), .clr(clr));
  Register #(.width(32)) R2 (.D(WD3), .en(decoder_1_out2), .Q(R2_q), .clk(clk), .clr(clr));
  Register #(.width(32)) R1 (.D(WD3), .en(decoder_1_out1), .Q(R1_q), .clk(clk), .clr(clr));
  Register #(.width(32)) R0 (.D(WD3), .en(decoder_1_out0), .Q(R0_q), .clk(clk), .clr(clr));
  Multiplexer #(.select(4), .width(32), .enable("false")) multiplexer_1 (
    .in0(R0_q), .in1(R1_q), .in2(R2_q), .in3(R3_q), .in4(R4_q), .in5(R5_q), .in6(R6_q), .in7(R7_q),
    .in8(R8_q), .in9(R9_q), .in10(R10_q), .in11(R11_q), .in12(R12_q), .in13(R13_q), .in14(R14_q), .in15(R15),
    .out(RD1), .sel(A1));
  Multiplexer #(.select(4), .width(32), .enable("false")) multiplexer_2 (
    .in0(R0_q), .in1(R1_q), .in2(R2_q), .in3(R3_q), .in4(R4_q), .in5(R5_q), .in6(R6_q), .in7(R7_q),
    .in8(R8_q), .in9(R9_q), .in10(R10_q), .in11(R11_q), .in12(R12_q), .in13(R13_q), .in14(R14_q), .out(RD2),
    .sel(A2));  // open: in15
endmodule

module ALU_Decoder (
  input  ALUOp,
  input  [5:0] Func_5_0,
  output [1:0] FlagW_1_0,
  output [1:0] out_4
);

  wire and_2_out, and_3_out, and_4_out, and_5_out;

  and and_1 (FlagW_1_0[1], ALUOp, Func_5_0[0]);
  and and_2 (and_2_out, ALUOp, ~Func_5_0[1], Func_5_0[2], ~Func_5_0[3], ~Func_5_0[4]);  // AND_Gate
  and and_3 (and_3_out, ALUOp, ~Func_5_0[1], ~Func_5_0[2], Func_5_0[3], Func_5_0[4]);  // AND_Gate
  and and_4 (and_4_out, ALUOp, ~Func_5_0[1], ~Func_5_0[2], ~Func_5_0[3], ~Func_5_0[4]);  // AND_Gate
  and and_5 (and_5_out, ALUOp, ~Func_5_0[1], ~Func_5_0[2], Func_5_0[3], Func_5_0[4]);  // AND_Gate
  or or_1 (out_4[0], and_2_out, and_3_out);
  or or_2 (out_4[1], and_4_out, and_5_out);
  and and_6 (FlagW_1_0[0], FlagW_1_0[1], ~out_4[1]);  // AND_Gate

  // Notes on the sheet:
  //   ALUControl 1:0
endmodule

module Main_Decoder (
  input  [1:0] Op_1_0,
  input  [5:0] Func_5_0,
  output Branch,
  output RegW,
  output MemW,
  output MemToReg,
  output ALUSrc,
  output [1:0] ImmSrc,
  output [1:0] RegSrc,
  output Aluop
);

  wire and_4_out, and_5_out, and_8_out, and_9_out, and_10_out;

  and and_1 (Branch, ~Op_1_0[0], Op_1_0[1]);  // AND_Gate
  and and_2 (MemToReg, Op_1_0[0], ~Op_1_0[1], Func_5_0[0]);  // AND_Gate
  and and_3 (MemW, Op_1_0[0], ~Op_1_0[1], ~Func_5_0[0]);  // AND_Gate
  and and_4 (and_4_out, ~Op_1_0[1], Func_5_0[5]);  // AND_Gate
  and and_5 (and_5_out, ~Op_1_0[0], Op_1_0[1]);  // AND_Gate
  and and_6 (ImmSrc[0], Op_1_0[0], ~Op_1_0[1]);  // AND_Gate
  and and_7 (Aluop, ~Op_1_0[0], ~Op_1_0[1]);  // AND_Gate
  and and_8 (and_8_out, Func_5_0[0], ~Op_1_0[1]);  // AND_Gate
  and and_9 (and_9_out, Op_1_0[0], ~Op_1_0[1], ~Func_5_0[5], ~Func_5_0[0]);  // AND_Gate
  and and_10 (and_10_out, Op_1_0[0], ~Op_1_0[1], Func_5_0[5], ~Func_5_0[0]);  // AND_Gate
  or or_1 (RegSrc[1], and_9_out, and_10_out);
  or or_2 (ALUSrc, and_4_out, and_5_out, ImmSrc[0]);
  or or_3 (RegW, Aluop, and_8_out);

  assign ImmSrc[1] = Branch;
  assign RegSrc[0] = Branch;
endmodule

module Decoder (
  input  [3:0] Rd3_0,
  input  [1:0] Op1_0,
  input  [5:0] Funct5_0,
  output PCS,
  output RegW,
  output MemW,
  output MemtoReg,
  output ALUSrc,
  output [1:0] ImmSrc1_0,
  output [1:0] FlagW1_0,
  output [1:0] RegSrc1_0,
  output [1:0] ALUControl1_0
);

  wire main_decoder_1_aluop, main_decoder_1_branch;

  Main_Decoder main_decoder_1 (
    .Op_1_0(Op1_0), .Func_5_0(Funct5_0), .Branch(main_decoder_1_branch), .RegW(RegW), .MemW(MemW),
    .MemToReg(MemtoReg), .ALUSrc(ALUSrc), .ImmSrc(ImmSrc1_0), .RegSrc(RegSrc1_0), .Aluop(main_decoder_1_aluop));
  ALU_Decoder alu_decoder_1 (
    .ALUOp(main_decoder_1_aluop), .Func_5_0(Funct5_0), .FlagW_1_0(FlagW1_0), .out_4(ALUControl1_0));
  PC_Logic pc_logic_1 (.Branch(main_decoder_1_branch), .RegW(RegW), .Rd_3_0(Rd3_0), .PCS(PCS));

  // Notes on the sheet:
  //   Main Decoder
  //   ALU Decoder
  //   PC Logic
endmodule

module PC_Logic (
  input  Branch,
  input  RegW,
  input  [3:0] Rd_3_0,
  output PCS
);

  wire and_1_out, comparator_1_eq;

  Comparator #(.width(4)) comparator_1 (.a(Rd_3_0), .b(4'b1111), .eq(comparator_1_eq));  // open: gt, lt
  and and_1 (and_1_out, RegW, comparator_1_eq);
  xor xor_1 (PCS, Branch, and_1_out);

  // Notes on the sheet:
  //   15
  //   Comparator
endmodule

module Conditional_Logic (
  input  PCS,
  input  RegW,
  input  MemW,
  input  [1:0] FlagW_1_0,
  input  [3:0] Cond_3_0,
  input  [3:0] ALU_Flags_3_0,
  input  CLK,
  input  CLR,
  output PCSrc,
  output RegWrite,
  output MemWrite
);

  wire and_1_out, and_2_out, condition_check_1_condex;
  wire [1:0] register_1_q, register_2_q;

  Register #(.width(2)) register_1 (.D(ALU_Flags_3_0[3:2]), .en(and_2_out), .Q(register_1_q), .clk(CLK), .clr(CLR));
  Register #(.width(2)) register_2 (.D(ALU_Flags_3_0[1:0]), .en(and_1_out), .Q(register_2_q), .clk(CLK), .clr(CLR));
  and and_1 (and_1_out, FlagW_1_0[0], condition_check_1_condex);
  and and_2 (and_2_out, FlagW_1_0[1], condition_check_1_condex);
  and and_3 (PCSrc, PCS, condition_check_1_condex);
  and and_4 (RegWrite, RegW, condition_check_1_condex);
  and and_5 (MemWrite, MemW, condition_check_1_condex);
  Condition_Check condition_check_1 (
    .Cond_3_0(Cond_3_0), .ALU_Flags_3_0({register_1_q, register_2_q}), .CondEx(condition_check_1_condex));

  // Notes on the sheet:
  //   Condition Check
endmodule

module Control_Unit (
  input  [3:0] Cond_3_0,
  input  [3:0] ALU_Flags_3_0,
  input  [3:0] Rd3_0,
  input  [1:0] Op1_0,
  input  [5:0] Funct5_0,
  input  CLK,
  input  CLR,
  output PCSrc,
  output RegWrite,
  output MemWrite,
  output MemtoReg,
  output ALUSrc,
  output [1:0] ImmSrc1_0,
  output [1:0] RegSrc1_0,
  output [1:0] ALUControl1_0
);

  wire decoder_1_memw, decoder_1_pcs, decoder_1_regw;
  wire [1:0] decoder_1_flagw1_0;

  Decoder decoder_1 (
    .Rd3_0(Rd3_0), .Op1_0(Op1_0), .Funct5_0(Funct5_0), .PCS(decoder_1_pcs), .RegW(decoder_1_regw),
    .MemW(decoder_1_memw), .MemtoReg(MemtoReg), .ALUSrc(ALUSrc), .ImmSrc1_0(ImmSrc1_0),
    .FlagW1_0(decoder_1_flagw1_0), .RegSrc1_0(RegSrc1_0), .ALUControl1_0(ALUControl1_0));
  Conditional_Logic conditional_logic_1 (
    .PCS(decoder_1_pcs), .RegW(decoder_1_regw), .MemW(decoder_1_memw), .FlagW_1_0(decoder_1_flagw1_0),
    .Cond_3_0(Cond_3_0), .ALU_Flags_3_0(ALU_Flags_3_0), .CLK(CLK), .CLR(CLR), .PCSrc(PCSrc),
    .RegWrite(RegWrite), .MemWrite(MemWrite));

  // Notes on the sheet:
  //   Decoder
  //   Conditional Logic
endmodule

module Condition_Check (
  input  [3:0] Cond_3_0,
  input  [3:0] ALU_Flags_3_0,
  output CondEx
);

  wire and_1_out, and_2_out, and_3_out;

  and and_1 (and_1_out, ~Cond_3_0[0], ~Cond_3_0[1], ~Cond_3_0[2], ~Cond_3_0[3], ALU_Flags_3_0[2]);  // AND_Gate
  and and_2 (and_2_out, ~Cond_3_0[0], Cond_3_0[1], Cond_3_0[2], Cond_3_0[3]);  // AND_Gate
  and and_3 (and_3_out, Cond_3_0[0], ~Cond_3_0[1], ~Cond_3_0[2], ~Cond_3_0[3], ~ALU_Flags_3_0[2]);  // AND_Gate
  or or_1 (CondEx, and_1_out, and_3_out, and_2_out);
endmodule

module ALU (
  input  [31:0] A,
  input  [31:0] B,
  input  [1:0] ALUControl,
  output [31:0] ALU_Result,
  output [3:0] ALU_Flags
);

  wire adder_1_cout, not_1_out, or_2_out, subtractor_1_bout, xnor_1_out, xor_1_out;
  wire [31:0] adder_1_out, and_1_out, or_1_out, subtractor_1_out;

  Adder #(.width(32)) adder_1 (.a(B), .b(A), .out(adder_1_out), .cout(adder_1_cout));  // open: cin
  Subtractor #(.width(32)) subtractor_1 (.a(A), .b(B), .out(subtractor_1_out), .bout(subtractor_1_bout));  // open: bin
  assign and_1_out = B & A;  // AND_Gate and_1, 32 bits wide
  assign or_1_out = B | A;  // OR_Gate or_1, 32 bits wide
  Multiplexer #(.select(2), .width(32), .enable("false")) multiplexer_1 (
    .in0(adder_1_out), .in1(subtractor_1_out), .in2(and_1_out), .in3(or_1_out),
    .out({ALU_Flags[3], ALU_Result[30:0]}), .sel(ALUControl));
  Comparator #(.width(32)) comparator_1 (
    .a({ALU_Flags[3], ALU_Result[30:0]}), .b({32{1'b0}}), .eq(ALU_Flags[2]));  // open: gt, lt
  NotExactlyOne xnor_1 (.out(xnor_1_out), .in0(A[31]), .in1(B[31]), .in2(ALUControl[0]));
  not not_1 (not_1_out, ALUControl[1]);
  xor xor_1 (xor_1_out, B[31], adder_1_out[31]);
  and and_2 (ALU_Flags[1], xnor_1_out, xor_1_out, not_1_out);
  or or_2 (or_2_out, subtractor_1_bout, adder_1_cout);
  and and_3 (ALU_Flags[0], not_1_out, or_2_out);

  assign ALU_Result[31] = ALU_Flags[3];

  // Other names for the same wires on the sheet: C = ALU_Flags[0]; V = ALU_Flags[1]; Z = ALU_Flags[2];
  //   N = ALU_Flags[3]; ALU_Control_0 = ALUControl[0]; ALU_Control_1 = ALUControl[1]
endmodule

module Extender (
  input  [1:0] in_1,
  input  [7:0] in_2,
  input  [11:0] in_3,
  input  [23:0] in_4,
  output [31:0] out_5
);

  wire [31:0] bit_extender_1_out, bit_extender_2_out, bit_extender_3_out, multiplier_1_out;

  assign bit_extender_1_out = {{24{1'b0}}, in_2};  // Bit_Extender bit_extender_1
  assign bit_extender_2_out = {{20{1'b0}}, in_3};  // Bit_Extender bit_extender_2
  assign bit_extender_3_out = {{8{in_4[23]}}, in_4};  // Bit_Extender bit_extender_3
  Multiplier #(.width(32)) multiplier_1 (.a(bit_extender_3_out), .b(32'h4), .out(multiplier_1_out));  // open: cin, cout
  Multiplexer #(.select(2), .width(32)) multiplexer_1 (
    .in0(bit_extender_1_out), .in1(bit_extender_2_out), .in2(multiplier_1_out), .out(out_5), .sel(in_1));  // open: in3, en
endmodule
