// Logisim project MAIN DECODER.circ as structural Verilog: 1 circuit, main circuit MainDecoder
module MainDecoder (
  input  [1:0] Op_1_0,
  input  [5:0] Func_5_0,
  output Branch,
  output RegW,
  output MemW,
  output MemToReg,
  output ALUSrc,
  output [1:0] ImmSrc,
  output [1:0] RegSrc,
  output Aluop
);

  wire and_4_out, and_5_out, and_8_out, and_9_out, and_10_out;

  and and_1 (Branch, ~Op_1_0[0], Op_1_0[1]);  // AND_Gate
  and and_2 (MemToReg, Op_1_0[0], ~Op_1_0[1], Func_5_0[0]);  // AND_Gate
  and and_3 (MemW, Op_1_0[0], ~Op_1_0[1], ~Func_5_0[0]);  // AND_Gate
  and and_4 (and_4_out, ~Op_1_0[1], Func_5_0[5]);  // AND_Gate
  and and_5 (and_5_out, ~Op_1_0[0], Op_1_0[1]);  // AND_Gate
  and and_6 (ImmSrc[0], Op_1_0[0], ~Op_1_0[1]);  // AND_Gate
  and and_7 (Aluop, ~Op_1_0[0], ~Op_1_0[1]);  // AND_Gate
  and and_8 (and_8_out, Func_5_0[0], ~Op_1_0[1]);  // AND_Gate
  and and_9 (and_9_out, Op_1_0[0], ~Op_1_0[1], ~Func_5_0[5], ~Func_5_0[0]);  // AND_Gate
  and and_10 (and_10_out, Op_1_0[0], ~Op_1_0[1], Func_5_0[5], ~Func_5_0[0]);  // AND_Gate
  or or_1 (RegSrc[1], and_9_out, and_10_out);
  or or_2 (ALUSrc, and_4_out, and_5_out, ImmSrc[0]);
  or or_3 (RegW, Aluop, and_8_out);

  assign ImmSrc[1] = Branch;
  assign RegSrc[0] = Branch;
endmodule
